// Logisim project mips-like.circ as structural Verilog: 5 circuits, main circuit PROCESSADOR
module PROCESSADOR (
  output [31:0] \INSTRUÇÃO 
);

  wire and_1_out, button_1_out, clock_1_out, UC_branch, UC_jump, UC_memread, UC_memtoreg, UC_memwrite,
       UC_regdst, UC_regwrite, UC_ula_src;
  wire [1:0] UC_ula_op1;
  wire [3:0] multiplexer_4_out;
  wire [7:0] PC_q_2;
  wire [19:0] ula_1_ula_out;
  wire [31:0] adder_1_out, banco_de_registradores_1_r0_d, banco_de_registradores_1_r1_d, multiplexer_1_out,
       multiplexer_2_out, multiplexer_3_out, multiplexer_5_out, multiplexer_6_out, PC_q, ram_1_data,
       rep_16_32_1_saida;
  wire [31:20] ula_1_ula_out_2;

  Adder #(.width(32)) adder_1 (.a({PC_q[31:10], PC_q_2, PC_q[1:0]}), .b(32'h4), .out(adder_1_out));  // open: cin, cout
  Multiplexer #(.width(32)) multiplexer_1 (
    .in0(rep_16_32_1_saida), .in1(multiplexer_3_out), .out(multiplexer_1_out), .sel(UC_branch));  // open: en
  Multiplexer #(.width(32)) multiplexer_2 (
    .in0(adder_1_out), .in1(multiplexer_1_out), .out(multiplexer_2_out), .sel(UC_jump));  // open: en
  Multiplexer #(.width(32)) multiplexer_3 (
    .in0({PC_q[31:10], PC_q_2, PC_q[1:0]}), .in1(rep_16_32_1_saida), .out(multiplexer_3_out), .sel(and_1_out));  // open: en
  Register #(.width(32)) PC (
    .D(multiplexer_2_out), .Q({PC_q[31:10], PC_q_2, PC_q[1:0]}), .clk(clock_1_out), .clr(button_1_out));  // open: en
  Clock clock_1 (.out(clock_1_out));
  Button button_1 (.out(button_1_out));
  and and_1 (and_1_out, 1'b1, ula_1_ula_out[0]);
  rep_16_32 rep_16_32_1 (.entrada(\INSTRUÇÃO [15:0]), .saida(rep_16_32_1_saida));
  ROM #(.dataWidth(32)) rom_1 (.addr(PC_q_2), .data(\INSTRUÇÃO ));  // open: sel
  UC UC (
    .E3(\INSTRUÇÃO [31]), .E2(\INSTRUÇÃO [30]), .E1(\INSTRUÇÃO [29]), .E0(\INSTRUÇÃO [28]),
    .RegDst(UC_regdst), .jump(UC_jump), .branch(UC_branch), .MemRead(UC_memread), .MemToReg(UC_memtoreg),
    .ula_op0(UC_ula_op1[1]), .ula_op1(UC_ula_op1[0]), .MemWrite(UC_memwrite), .ula_src(UC_ula_src),
    .RegWrite(UC_regwrite));
  Multiplexer #(.width(4)) multiplexer_4 (
    .in0(\INSTRUÇÃO [23:20]), .in1(\INSTRUÇÃO [27:24]), .out(multiplexer_4_out), .sel(UC_regdst));  // open: en
  BANCO_DE_REGISTRADORES banco_de_registradores_1 (
    .DATA_WRITE(multiplexer_6_out), .CLK(clock_1_out), .RW(multiplexer_4_out),
    .R0_D(banco_de_registradores_1_r0_d), .R0(\INSTRUÇÃO [19:16]), .R1_D(banco_de_registradores_1_r1_d),
    .R1(\INSTRUÇÃO [23:20]), .RW_2(UC_regwrite), .RESET(button_1_out));
  Multiplexer #(.width(32)) multiplexer_5 (
    .in0(banco_de_registradores_1_r1_d), .in1({{28{1'b0}}, \INSTRUÇÃO [19:16]}), .out(multiplexer_5_out),
    .sel(UC_ula_src));  // open: en
  ULA ula_1 (
    .DATA_0(banco_de_registradores_1_r0_d), .DATA_1(multiplexer_5_out),
    .ULA_OUT({ula_1_ula_out_2, ula_1_ula_out}), .ULA_OP(UC_ula_op1));
  RAM #(.addrWidth(20), .dataWidth(32), .bus("separate")) ram_1 (
    .addr(ula_1_ula_out), .din(banco_de_registradores_1_r1_d), .data(ram_1_data), .str(UC_memwrite),
    .ld(UC_memread));  // open: sel, clk, clr
  Multiplexer #(.width(32)) multiplexer_6 (
    .in0({ula_1_ula_out_2, ula_1_ula_out}), .in1(ram_1_data), .out(multiplexer_6_out), .sel(UC_memtoreg));  // open: en

  // Notes on the sheet:
  //   REG_0
  //   REG_1
  //   REG_W
  //   contents of rom_1 (hex, n*v repeats v):
  //   20020000 0 0 0 80000000 35*0 1000
  //   DATA_W
  //   BANCO DE REGISTRADORES
  //   REG0_D
  //   REG1_D
  //   ULA
endmodule

module ULA (
  input  [31:0] DATA_0,
  input  [31:0] DATA_1,
  input  [1:0] ULA_OP,
  output [31:0] ULA_OUT
);

  wire comparator_1_eq, comparator_1_gt;
  wire [31:0] adder_1_out, multiplier_1_out, shifter_1_out;
  wire [31:31] or_1_out;

  Adder #(.width(32)) adder_1 (.a(DATA_0), .b(DATA_1), .out(adder_1_out));  // open: cin, cout
  Multiplier #(.width(32)) multiplier_1 (.a(DATA_0), .b(DATA_1), .out(multiplier_1_out));  // open: cin, cout
  Comparator #(.width(32), .mode("unsigned")) comparator_1 (
    .a(DATA_0), .b(DATA_1), .gt(comparator_1_gt), .eq(comparator_1_eq));  // open: lt
  or or_1 (or_1_out[31], comparator_1_gt, comparator_1_eq);
  Shifter #(.width(32)) shifter_1 (.in(DATA_0), .\dist (DATA_1[4:0]), .out(shifter_1_out));
  Multiplexer #(.select(2), .width(32), .enable("false")) multiplexer_1 (
    .in0(adder_1_out), .in1(multiplier_1_out), .in2({32{or_1_out[31]}}), .in3(shifter_1_out), .out(ULA_OUT),
    .sel(ULA_OP));
endmodule

module UC (
  input  E3,
  input  E2,
  input  E1,
  input  E0,
  output RegDst,
  output jump,
  output branch,
  output MemRead,
  output MemToReg,
  output ula_op0,
  output ula_op1,
  output MemWrite,
  output ula_src,
  output RegWrite
);

  wire and_1_out, and_2_out, and_3_out, and_4_out, and_5_out, and_6_out, and_7_out, and_8_out, and_9_out,
       and_10_out, and_11_out, and_12_out, and_13_out, and_14_out, and_15_out, and_16_out, and_17_out,
       and_18_out, and_19_out, and_20_out, not_1_out, not_2_out, not_3_out, not_4_out, not_5_out, not_6_out,
       not_7_out, not_8_out, not_9_out, not_10_out, not_11_out, not_12_out, not_13_out, not_14_out,
       not_15_out, not_16_out, not_17_out, not_18_out, not_19_out, not_20_out, not_21_out, not_22_out,
       not_23_out, not_24_out, not_25_out, not_26_out, not_27_out, not_28_out;

  not not_1 (not_1_out, E3);
  and and_1 (and_1_out, not_1_out, not_2_out);
  not not_2 (not_2_out, E2);
  not not_3 (not_3_out, E2);
  and and_2 (and_2_out, not_3_out, E1);
  and and_3 (and_3_out, E3, not_4_out, E0);
  not not_4 (not_4_out, E1);
  and and_4 (and_4_out, E3, E1, not_5_out);
  not not_5 (not_5_out, E0);
  and and_5 (and_5_out, E3, E2);
  not not_6 (not_6_out, E1);
  and and_6 (and_6_out, E2, not_6_out, not_7_out);
  not not_7 (not_7_out, E0);
  and and_7 (and_7_out, E3, E2, not_8_out);
  not not_8 (not_8_out, E0);
  and and_8 (and_8_out, E2, not_9_out, not_10_out);
  not not_9 (not_9_out, E1);
  not not_10 (not_10_out, E0);
  and and_9 (and_9_out, E3, E2, not_11_out);
  not not_11 (not_11_out, E0);
  not not_12 (not_12_out, E2);
  and and_10 (and_10_out, not_12_out, E1, not_13_out);
  not not_13 (not_13_out, E0);
  and and_11 (and_11_out, E3, not_14_out);
  not not_14 (not_14_out, E0);
  not not_15 (not_15_out, E3);
  not not_16 (not_16_out, E2);
  not not_17 (not_17_out, E1);
  not not_18 (not_18_out, E2);
  not not_19 (not_19_out, E0);
  not not_20 (not_20_out, E0);
  not not_21 (not_21_out, E3);
  not not_22 (not_22_out, E2);
  not not_23 (not_23_out, E0);
  not not_24 (not_24_out, E3);
  and and_12 (and_12_out, not_24_out, E1);
  and and_13 (and_13_out, E3, E0);
  not not_25 (not_25_out, E3);
  and and_14 (and_14_out, not_25_out, not_26_out);
  not not_26 (not_26_out, E2);
  not not_27 (not_27_out, E3);
  and and_15 (and_15_out, not_27_out, not_28_out);
  not not_28 (not_28_out, E0);
  or or_1 (RegDst, and_1_out, and_2_out);
  or or_2 (branch, and_3_out, and_4_out, and_5_out);
  or or_3 (MemRead, and_6_out, and_7_out);
  or or_4 (MemToReg, and_8_out, and_9_out);
  or or_5 (ula_op0, and_10_out, and_11_out);
  and and_16 (and_16_out, not_15_out, not_16_out, not_17_out, E0);
  or or_6 (ula_op1, and_16_out, and_17_out, and_18_out);
  and and_17 (and_17_out, not_18_out, E1, not_19_out);
  and and_18 (and_18_out, E3, E2, not_20_out);
  and and_19 (and_19_out, not_21_out, E2, E0);
  or or_7 (MemWrite, and_19_out, and_20_out);
  and and_20 (and_20_out, E3, not_22_out, E1, not_23_out);
  or or_8 (ula_src, and_12_out, E2, and_13_out);
  or or_9 (RegWrite, and_14_out, and_15_out);

  assign jump = E3;
endmodule

module BANCO_DE_REGISTRADORES (
  input  [31:0] DATA_WRITE,
  input  [3:0] R0,
  input  CLK,
  input  [3:0] R1,
  input  [3:0] RW,
  input  RESET,
  input  RW_2,
  output [31:0] R0_D,
  output [31:0] R1_D
);

  wire demultiplexer_1_out0, demultiplexer_1_out1, demultiplexer_1_out2, demultiplexer_1_out3;
  wire [31:0] register_1_q, register_2_q, register_3_q, register_4_q;

  Demultiplexer #(.select(2), .enable("false")) demultiplexer_1 (
    .out0(demultiplexer_1_out0), .out1(demultiplexer_1_out1), .out2(demultiplexer_1_out2),
    .out3(demultiplexer_1_out3), .in(RW_2), .sel(RW[1:0]));
  Register #(.width(32)) register_1 (
    .D(DATA_WRITE), .en(demultiplexer_1_out0), .Q(register_1_q), .clk(CLK), .clr(RESET));
  Register #(.width(32)) register_2 (
    .D(DATA_WRITE), .en(demultiplexer_1_out1), .Q(register_2_q), .clk(CLK), .clr(RESET));
  Register #(.width(32)) register_3 (
    .D(DATA_WRITE), .en(demultiplexer_1_out2), .Q(register_3_q), .clk(CLK), .clr(RESET));
  Register #(.width(32)) register_4 (
    .D(DATA_WRITE), .en(demultiplexer_1_out3), .Q(register_4_q), .clk(CLK), .clr(RESET));
  Multiplexer #(.select(2), .width(32), .disabled(0), .enable("false")) multiplexer_1 (
    .in0(register_1_q), .in1(register_2_q), .in2(register_3_q), .in3(register_4_q), .out(R0_D), .sel(R0[1:0]));
  Multiplexer #(.select(2), .width(32), .enable("false")) multiplexer_2 (
    .in0(register_1_q), .in1(register_2_q), .in2(register_3_q), .in3(register_4_q), .out(R1_D), .sel(R1[1:0]));
endmodule

module rep_16_32 (
  input  [15:0] entrada,
  output [31:0] saida
);


  assign saida = {{16{1'b0}}, entrada};
endmodule
